// Logisim project 4-Bitwise Not Circuit-DL Lab 1.circ as structural Verilog: 1 circuit, main circuit main
module main (
  input  [3:0] in_1,
  output [3:0] out_2
);

  not not_1 (out_2[2], in_1[2]);
  not not_2 (out_2[3], in_1[3]);
  not not_3 (out_2[0], in_1[0]);
  not not_4 (out_2[1], in_1[1]);

  // Notes on the sheet:
  //   4-Bitwise Not Circuit
endmodule
