// Logisim project 4-Bit Adder.circ as structural Verilog: 1 circuit, main circuit main
module main (
  input  Cin,
  input  [3:0] A,
  input  [3:0] B,
  output [3:0] Sum,
  output out_5
);

  Adder #(.width(4)) adder_1 (.a(A), .b(B), .out(Sum), .cin(Cin), .cout(out_5));

  // Notes on the sheet:
  //   Cout
endmodule
