// Logisim project Four Bit Full Adder.circ as structural Verilog: 1 circuit, main circuit main
module main (
  input  [3:0] A,
  input  [3:0] B,
  input  Cin,
  output Cout,
  output [3:0] Sum
);

  wire and_1_out, and_2_out, and_3_out, and_4_out, and_5_out, and_6_out, and_7_out, and_8_out, and_9_out,
       and_10_out, and_11_out, and_12_out, or_2_out, or_3_out, or_4_out, xor_1_out, xor_3_out, xor_5_out,
       xor_7_out;

  or or_1 (Cout, and_1_out, and_2_out, and_3_out);
  and and_1 (and_1_out, A[3], B[3]);
  and and_2 (and_2_out, or_2_out, A[3]);
  and and_3 (and_3_out, or_2_out, B[3]);
  xor xor_1 (xor_1_out, A[3], B[3]);
  or or_2 (or_2_out, and_4_out, and_5_out, and_6_out);
  xor xor_2 (Sum[3], xor_1_out, or_2_out);
  and and_4 (and_4_out, A[2], B[2]);
  and and_5 (and_5_out, or_3_out, A[2]);
  and and_6 (and_6_out, or_3_out, B[2]);
  or or_3 (or_3_out, and_7_out, and_8_out, and_9_out);
  xor xor_3 (xor_3_out, A[2], B[2]);
  xor xor_4 (Sum[2], xor_3_out, or_3_out);
  and and_7 (and_7_out, A[1], B[1]);
  and and_8 (and_8_out, or_4_out, A[1]);
  and and_9 (and_9_out, or_4_out, B[1]);
  xor xor_5 (xor_5_out, A[1], B[1]);
  or or_4 (or_4_out, and_10_out, and_11_out, and_12_out);
  xor xor_6 (Sum[1], xor_5_out, or_4_out);
  and and_10 (and_10_out, A[0], B[0]);
  and and_11 (and_11_out, Cin, A[0]);
  and and_12 (and_12_out, Cin, B[0]);
  xor xor_7 (xor_7_out, A[0], B[0]);
  xor xor_8 (Sum[0], xor_7_out, Cin);

  // Notes on the sheet:
  //   A
  //   B
  //   A
  //   B
  //   A
  //   B
  //   A
  //   B
endmodule
