// Logisim project One Bit Full Adder.circ as structural Verilog: 1 circuit, main circuit main
module main (
  input  A,
  input  B,
  input  Cin,
  output Cout,
  output Sum
);

  wire and_1_out, and_2_out, and_3_out, xor_1_out;

  or or_1 (Cout, and_1_out, and_2_out, and_3_out);
  and and_1 (and_1_out, A, B);
  and and_2 (and_2_out, Cin, A);
  and and_3 (and_3_out, Cin, B);
  xor xor_1 (xor_1_out, A, B);
  xor xor_2 (Sum, xor_1_out, Cin);

  // Notes on the sheet:
  //   One Bit Full Adder
endmodule
