// Logisim project One Bit Half Adder.circ as structural Verilog: 1 circuit, main circuit main
module main (
  input  in_1,
  input  in_2,
  output out_3,
  output Sum
);

  and and_1 (out_3, in_1, in_2);
  xor xor_1 (Sum, in_1, in_2);

  // Notes on the sheet:
  //   And
  //   Cout
  //   One Bit Half Adder
  //   Xor
endmodule
