// Logisim project Multiplexer.circ as structural Verilog: 1 circuit, main circuit main
module main (
  input  in_1,
  input  [3:0] in_2,
  input  [3:0] in_3
);

  wire and_1_out, and_2_out, and_3_out, and_4_out, and_5_out, and_6_out, and_7_out, and_8_out, not_1_out,
       or_1_out, or_2_out, or_3_out, or_4_out;
  wire [3:0] multiplexer_1_out;

  not not_1 (not_1_out, in_1);
  and and_1 (and_1_out, not_1_out, in_2[3]);
  and and_2 (and_2_out, not_1_out, in_2[2]);
  and and_3 (and_3_out, not_1_out, in_2[1]);
  and and_4 (and_4_out, not_1_out, in_2[0]);
  or or_1 (or_1_out, and_1_out, and_5_out);
  LED led_1 (.in(or_1_out));
  or or_2 (or_2_out, and_2_out, and_6_out);
  LED led_2 (.in(or_2_out));
  and and_5 (and_5_out, in_1, in_3[3]);
  or or_3 (or_3_out, and_3_out, and_8_out);
  LED led_3 (.in(or_3_out));
  and and_6 (and_6_out, in_1, in_3[2]);
  or or_4 (or_4_out, and_4_out, and_7_out);
  LED led_4 (.in(or_4_out));
  and and_7 (and_7_out, in_1, in_3[0]);
  and and_8 (and_8_out, in_1, in_3[1]);
  LED led_5 (.in(multiplexer_1_out[2]));
  LED led_6 (.in(multiplexer_1_out[3]));
  Multiplexer #(.width(4), .enable("false")) multiplexer_1 (
    .in0(in_2), .in1(in_3), .out(multiplexer_1_out), .sel(in_1));
  LED led_7 (.in(multiplexer_1_out[0]));
  LED led_8 (.in(multiplexer_1_out[1]));
endmodule
