// Logisim project Octal_Decoder.circ as structural Verilog: 1 circuit, main circuit main
module main (
  input  [2:0] in_1
);

  wire and_1_out, and_2_out, and_3_out, and_4_out, and_5_out, and_6_out, and_7_out, and_8_out,
       decoder_1_out0, decoder_1_out1, decoder_1_out2, decoder_1_out3, decoder_1_out4, decoder_1_out5,
       decoder_1_out6, decoder_1_out7, not_1_out, not_2_out, not_3_out;

  not not_1 (not_1_out, in_1[1]);
  not not_2 (not_2_out, in_1[2]);
  not not_3 (not_3_out, in_1[0]);
  and and_1 (and_1_out, not_2_out, not_1_out, not_3_out);
  LED led_1 (.in(and_1_out));
  and and_2 (and_2_out, not_2_out, not_1_out, in_1[0]);
  LED led_2 (.in(and_2_out));
  and and_3 (and_3_out, not_2_out, in_1[1], not_3_out);
  LED led_3 (.in(and_3_out));
  LED led_4 (.in(and_4_out));
  and and_4 (and_4_out, not_2_out, in_1[1], in_1[0]);
  and and_5 (and_5_out, in_1[2], not_1_out, not_3_out);
  LED led_5 (.in(and_5_out));
  LED led_6 (.in(and_6_out));
  and and_6 (and_6_out, in_1[2], not_1_out, in_1[0]);
  and and_7 (and_7_out, in_1[2], in_1[1], not_3_out);
  LED led_7 (.in(and_7_out));
  LED led_8 (.in(and_8_out));
  and and_8 (and_8_out, in_1[2], in_1[1], in_1[0]);
  LED led_9 (.in(decoder_1_out2));
  LED led_10 (.in(decoder_1_out1));
  LED led_11 (.in(decoder_1_out0));
  Decoder #(.select(3), .enable("false")) decoder_1 (
    .out0(decoder_1_out0), .out1(decoder_1_out1), .out2(decoder_1_out2), .out3(decoder_1_out3),
    .out4(decoder_1_out4), .out5(decoder_1_out5), .out6(decoder_1_out6), .out7(decoder_1_out7), .sel(in_1));
  LED led_12 (.in(decoder_1_out4));
  LED led_13 (.in(decoder_1_out3));
  LED led_14 (.in(decoder_1_out6));
  LED led_15 (.in(decoder_1_out5));
  LED led_16 (.in(decoder_1_out7));

  // Notes on the sheet:
  //   L0
  //   L1
  //   L2
  //   L3
  //   L4
  //   L5
  //   L6
  //   L7
  //   L1
  //   L2
  //   L0
  //   L3
  //   L4
  //   L6
  //   L7
  //   L5
endmodule
