// Logisim project Octal_Decoder_AND_NOT.circ as structural Verilog: 1 circuit, main circuit main
module main (
  input  [2:0] in_1
);

  wire and_1_out, and_2_out, and_3_out, and_4_out, and_5_out, and_6_out, and_7_out, and_8_out, not_1_out,
       not_2_out, not_3_out;

  not not_1 (not_1_out, in_1[2]);
  not not_2 (not_2_out, in_1[1]);
  not not_3 (not_3_out, in_1[0]);
  and and_1 (and_1_out, not_1_out, not_2_out, not_3_out);
  LED led_1 (.in(and_1_out));
  and and_2 (and_2_out, not_1_out, not_2_out, in_1[0]);
  LED led_2 (.in(and_2_out));
  and and_3 (and_3_out, not_1_out, in_1[1], not_3_out);
  LED led_3 (.in(and_3_out));
  LED led_4 (.in(and_4_out));
  and and_4 (and_4_out, not_1_out, in_1[1], in_1[0]);
  and and_5 (and_5_out, in_1[2], not_2_out, not_3_out);
  LED led_5 (.in(and_5_out));
  and and_6 (and_6_out, in_1[2], not_2_out, in_1[0]);
  LED led_6 (.in(and_6_out));
  LED led_7 (.in(and_7_out));
  and and_7 (and_7_out, in_1[2], in_1[1], not_3_out);
  LED led_8 (.in(and_8_out));
  and and_8 (and_8_out, in_1[2], in_1[1], in_1[0]);

  // Notes on the sheet:
  //   L0
  //   L1
  //   L2
  //   L3
  //   L4
  //   L5
  //   L6
  //   L7
endmodule
