// Logisim project Tiny_ALU.circ as structural Verilog: 1 circuit, main circuit main
module main (
  input  [1:0] in_1,
  input  [7:0] in_2,
  output [7:0] out_3
);

  wire and_1_out, and_2_out, and_3_out, and_4_out, and_5_out, and_6_out, and_7_out;
  wire [7:0] xor_1_out;

  xor xor_1 (xor_1_out[0], in_2[0], in_1[1]);
  xor xor_2 (xor_1_out[1], in_2[1], in_1[1]);
  xor xor_3 (xor_1_out[2], in_2[2], in_1[1]);
  xor xor_4 (xor_1_out[3], in_2[3], in_1[1]);
  xor xor_5 (xor_1_out[4], in_2[4], in_1[1]);
  xor xor_6 (xor_1_out[5], in_2[5], in_1[1]);
  xor xor_7 (xor_1_out[6], in_2[6], in_1[1]);
  xor xor_8 (xor_1_out[7], in_2[7], in_1[1]);
  and and_1 (and_1_out, xor_1_out[0], in_1[0]);
  and and_2 (and_2_out, xor_1_out[1], and_1_out);
  and and_3 (and_3_out, xor_1_out[2], and_2_out);
  and and_4 (and_4_out, xor_1_out[3], and_3_out);
  and and_5 (and_5_out, xor_1_out[4], and_4_out);
  and and_6 (and_6_out, xor_1_out[5], and_5_out);
  and and_7 (and_7_out, xor_1_out[6], and_6_out);
  xor xor_9 (out_3[0], in_1[0], xor_1_out[0]);
  xor xor_10 (out_3[1], and_1_out, xor_1_out[1]);
  xor xor_11 (out_3[2], and_2_out, xor_1_out[2]);
  xor xor_12 (out_3[3], and_3_out, xor_1_out[3]);
  xor xor_13 (out_3[4], and_4_out, xor_1_out[4]);
  xor xor_14 (out_3[5], and_5_out, xor_1_out[5]);
  xor xor_15 (out_3[6], and_6_out, xor_1_out[6]);
  xor xor_16 (out_3[7], and_7_out, xor_1_out[7]);
endmodule
