// Logisim project 8-Bit register transfer with adder.circ as structural Verilog: 1 circuit, main circuit main
module main (
  input  A,
  input  B,
  input  C,
  input  D,
  input  [1:0] Rmux,
  input  Dmux,
  input  Acc,
  input  Sub
);

  wire clock_1_out;
  wire [7:0] adder_1_out, multiplexer_1_out, multiplexer_2_out, register_1_q, register_2_q, register_3_q,
       register_4_q, register_5_q, xor_1_out;

  Clock clock_1 (.out(clock_1_out));
  Register register_1 (.D(register_5_q), .en(A), .Q(register_1_q), .clk(clock_1_out));  // open: clr
  Register register_2 (.D(register_5_q), .en(B), .Q(register_2_q), .clk(clock_1_out));  // open: clr
  Register register_3 (.D(register_5_q), .en(C), .Q(register_3_q), .clk(clock_1_out));  // open: clr
  Register register_4 (.D(register_5_q), .en(D), .Q(register_4_q), .clk(clock_1_out));  // open: clr
  Multiplexer #(.select(2), .width(8), .enable("false")) multiplexer_1 (
    .in0(register_1_q), .in1(register_2_q), .in2(register_3_q), .in3(register_4_q), .out(multiplexer_1_out),
    .sel(Rmux));
  Multiplexer #(.width(8), .enable("false")) multiplexer_2 (
    .in0(adder_1_out), .in1(multiplexer_1_out), .out(multiplexer_2_out), .sel(Dmux));
  Register register_5 (.D(multiplexer_2_out), .en(Acc), .Q(register_5_q), .clk(clock_1_out));  // open: clr
  assign xor_1_out = multiplexer_1_out ^ {8{Sub}};  // XOR_Gate xor_1, 8 bits wide
  Adder adder_1 (.a(register_5_q), .b(xor_1_out), .out(adder_1_out), .cin(Sub));  // open: cout

  // Notes on the sheet:
  //   A reg
  //   B reg
  //   C reg
  //   D reg
  //   8-Bit Register Transfer with Adder
  //   Acc
endmodule
