// Logisim project SAM part 1.circ as structural Verilog: 1 circuit, main circuit main
module main (
  input  Pc,
  input  Inc,
  input  Amux,
  input  Mar,
  input  Mst,
  input  Ir,
  input  Dmux,
  input  Acc,
  input  Out,
  input  Sub,
  output [7:0] out_11
);

  wire and_1_out, clock_1_out, Clr_out, Hlt_out;
  wire [3:0] IR_q, MAR_q, multiplexer_1_out, not_1_out, PC_q;
  wire [7:0] ACC_q, adder_1_out, multiplexer_2_out, ram_1_data, xor_1_out;
  wire [7:4] IR_q_2;

  Clock clock_1 (.out(clock_1_out));
  Button Clr (.out(Clr_out));
  and and_1 (and_1_out, clock_1_out, Hlt_out);
  Counter #(.width(4), .max('hf)) u_PC (
    .load(Pc), .D(IR_q), .count(Inc), .Q(PC_q), .clk(and_1_out));  // open: carry, clr
  Multiplexer #(.width(4), .enable("false")) multiplexer_1 (
    .in0(PC_q), .in1(IR_q), .out(multiplexer_1_out), .sel(Amux));
  Register #(.width(4)) u_MAR (.D(multiplexer_1_out), .en(Mar), .Q(MAR_q), .clk(and_1_out));  // open: clr
  RAM #(.addrWidth(4), .bus("separate")) ram_1 (
    .addr(MAR_q), .din(ACC_q), .data(ram_1_data), .str(Mst), .clk(and_1_out));  // open: sel, ld, clr
  Register u_IR (.D(ram_1_data), .en(Ir), .Q({IR_q_2, IR_q}), .clk(and_1_out), .clr(Clr_out));
  Multiplexer #(.width(8), .enable("false")) multiplexer_2 (
    .in0(adder_1_out), .in1(ram_1_data), .out(multiplexer_2_out), .sel(Dmux));
  Register u_ACC (.D(multiplexer_2_out), .en(Acc), .Q(ACC_q), .clk(and_1_out));  // open: clr
  nand Hlt (Hlt_out, IR_q_2[7], IR_q_2[6], IR_q_2[5], IR_q_2[4]);
  Register u_OUT (.D(ACC_q), .en(Out), .Q(out_11), .clk(and_1_out));  // open: clr
  assign xor_1_out = ram_1_data ^ {8{Sub}};  // XOR_Gate xor_1, 8 bits wide
  Adder adder_1 (.a(ACC_q), .b(xor_1_out), .out(adder_1_out), .cin(Sub));  // open: cout
  assign not_1_out = ~IR_q_2;  // NOT_Gate not_1, 4 bits wide

  // Notes on the sheet:
  //   SAM Datapath
endmodule
