// Logisim project SAM FINAL.circ as structural Verilog
module main (
  output [7:0] out_1,
  output Pc,
  output Inc,
  output Amux,
  output Mar,
  output Mst,
  output Ir,
  output Dmux,
  output Acc,
  output Out,
  output Sub
);

  wire Acc_2_out, Add_out, Amux_2_out, and_1_out, clock_1_out, Clr_out, decoder_1_out2, decoder_1_out3,
       Hlt_out, Jaz_2_out, Jaz_3_out, Jaz_out, Jmp_out, Lda_out, Mar_2_out, Mar_4_out, not_1_out, Out_3_out,
       Pc_2_out, Sta_out, Sub_2_out;
  wire [1:0] RT_State_q;
  wire [3:0] IR_q, MAR_3_q, multiplexer_1_out, not_2_out, PC_3_q;
  wire [7:0] ACC_3_q, adder_1_out, multiplexer_2_out, ram_1_data, xor_1_out;
  wire [7:4] IR_q_2;

  Clock clock_1 (.out(clock_1_out));
  Button Clr (.out(Clr_out));
  and and_1 (and_1_out, clock_1_out, Hlt_out);
  and u_Pc (Pc, decoder_1_out2, Pc_2_out);
  or Pc_2 (Pc_2_out, Jmp_out, Jaz_out);
  and Jaz (Jaz_out, Jaz_2_out, Jaz_3_out);
  not not_1 (not_1_out, and_1_out);
  nor Jaz_2 (Jaz_2_out, ACC_3_q[7], ACC_3_q[6], ACC_3_q[5], ACC_3_q[4], ACC_3_q[3], ACC_3_q[2], ACC_3_q[1], ACC_3_q[0]);
  Counter #(.width(4), .max('hf)) PC_3 (
    .load(Pc), .D(IR_q), .count(Inc), .Q(PC_3_q), .clk(and_1_out));  // open: carry, clr
  and u_Amux (Amux, decoder_1_out2, Amux_2_out);
  Counter #(.width(2), .max('h3)) RT_State (
    .Q(RT_State_q), .clk(not_1_out), .clr(Clr_out));  // open: load, D, count, carry
  Multiplexer #(.width(4), .enable("false")) multiplexer_1 (
    .in0(PC_3_q), .in1(IR_q), .out(multiplexer_1_out), .sel(Amux));
  or u_Mar (Mar, Inc, Mar_2_out);
  and Mar_2 (Mar_2_out, decoder_1_out2, Mar_4_out);
  or Amux_2 (Amux_2_out, Sta_out, Sub_2_out, Add_out, Lda_out);
  Decoder #(.select(2), .enable("false")) decoder_1 (
    .out0(Inc), .out1(Ir), .out2(decoder_1_out2), .out3(decoder_1_out3), .sel(RT_State_q));
  Register #(.width(4)) MAR_3 (.D(multiplexer_1_out), .en(Mar), .Q(MAR_3_q), .clk(and_1_out));  // open: clr
  and u_Mst (Mst, decoder_1_out3, Sta_out);
  or Mar_4 (Mar_4_out, Lda_out, Add_out, Sub_2_out, Sta_out);
  RAM #(.addrWidth(4), .bus("separate")) ram_1 (
    .addr(MAR_3_q), .din(ACC_3_q), .data(ram_1_data), .str(Mst), .clk(and_1_out));  // open: sel, ld, clr
  Register u_IR (.D(ram_1_data), .en(Ir), .Q({IR_q_2, IR_q}), .clk(and_1_out), .clr(Clr_out));
  and u_Dmux (Dmux, decoder_1_out3, Lda_out);
  and u_Acc (Acc, decoder_1_out3, Acc_2_out);
  Multiplexer #(.width(8), .enable("false")) multiplexer_2 (
    .in0(adder_1_out), .in1(ram_1_data), .out(multiplexer_2_out), .sel(Dmux));
  or Acc_2 (Acc_2_out, Lda_out, Add_out, Sub_2_out);
  Register ACC_3 (.D(multiplexer_2_out), .en(Acc), .Q(ACC_3_q), .clk(and_1_out));  // open: clr
  and u_Out (Out, decoder_1_out2, Out_3_out);
  and u_Sub (Sub, decoder_1_out3, Sub_2_out);
  Register OUT_2 (.D(ACC_3_q), .en(Out), .Q(out_1), .clk(and_1_out));  // open: clr
  and Lda (Lda_out, not_2_out[3], not_2_out[2], not_2_out[1], not_2_out[0]);
  and Add (Add_out, not_2_out[3], not_2_out[2], not_2_out[1], IR_q_2[4]);
  and Sub_2 (Sub_2_out, not_2_out[3], not_2_out[2], IR_q_2[5], not_2_out[0]);
  and Sta (Sta_out, not_2_out[3], not_2_out[2], IR_q_2[5], IR_q_2[4]);
  and Jmp (Jmp_out, not_2_out[3], IR_q_2[6], not_2_out[1], not_2_out[0]);
  and Jaz_3 (Jaz_3_out, not_2_out[3], IR_q_2[6], not_2_out[1], IR_q_2[4]);
  and Out_3 (Out_3_out, IR_q_2[7], IR_q_2[6], IR_q_2[5], not_2_out[0]);
  nand Hlt (Hlt_out, IR_q_2[7], IR_q_2[6], IR_q_2[5], IR_q_2[4]);
  assign xor_1_out = ram_1_data ^ {8{Sub}};  // XOR_Gate xor_1, 8 bits wide
  Adder adder_1 (.a(ACC_3_q), .b(xor_1_out), .out(adder_1_out), .cin(Sub));  // open: cout
  assign not_2_out = ~IR_q_2;  // NOT_Gate not_2, 4 bits wide

  // Notes on the sheet:
  //   SAM Datapath
  //   t0
  //   t1
  //   t2
  //   t3
endmodule
